// Logisim project logic_gates.circ as structural Verilog: 1 circuit, main circuit main
module main (
  input  A,
  input  B,
  input  C,
  input  D,
  input  E,
  input  F,
  input  G,
  input  H,
  output P,
  output Q,
  output R,
  output S
);

  and and_1 (P, A, B);
  nand nand_1 (Q, C, D);
  or or_1 (R, E, F);
  xor xor_1 (S, G, H);
endmodule
