// Logisim project seqCirc.circ as structural Verilog: 6 circuits, main circuit main
module main (
  input  sw,
  input  clk,
  input  reset,
  output led
);

  wire q0_q, q1_q, q2_q, seq_1_d0, seq_1_d1, seq_1_d2;

  seq seq_1 (.q2(q2_q), .q1(q1_q), .q0(q0_q), .sw(sw), .d2(seq_1_d2), .d1(seq_1_d1), .d0(seq_1_d0));
  D_Flip_Flop q2 (.D(seq_1_d2), .clk(clk), .Q(q2_q), .reset(reset));  // open: Qn, preset
  D_Flip_Flop q1 (.D(seq_1_d1), .clk(clk), .Q(q1_q), .reset(reset));  // open: Qn, preset
  D_Flip_Flop q0 (.D(seq_1_d0), .clk(clk), .Q(q0_q), .reset(reset));  // open: Qn, preset
  out_logic out_logic_1 (.q2(q2_q), .q1(q1_q), .q0(q0_q), .sw(sw), .E(led));
endmodule

module seq (
  input  q2,
  input  q1,
  input  q0,
  input  sw,
  output d2,
  output d1,
  output d0
);

  wire and_2_out, and_3_out, and_4_out, not_1_out, not_2_out, not_3_out;

  not not_1 (not_1_out, q2);
  not not_2 (not_2_out, q1);
  not not_3 (not_3_out, sw);
  and and_1 (d2, q1, not_3_out);
  and and_2 (and_2_out, not_1_out, not_2_out, q0);
  and and_3 (and_3_out, not_1_out, q0, sw);
  and and_4 (and_4_out, q1, q0);
  or or_1 (d1, and_2_out, and_3_out);
  or or_2 (d0, sw, and_4_out);
endmodule

module out_logic (
  input  q2,
  input  q1,
  input  q0,
  input  sw,
  output E
);

  wire not_1_out;

  not not_1 (not_1_out, sw);
  and and_1 (E, not_1_out, q2);
endmodule

module debounce_board (
  input  reset,
  input  tl_in,
  input  clk,
  output tl_out
);

  wire comparator_1_eq, comparator_2_eq;
  wire [18:0] counter_1_q;

  Counter #(.max('h7ffff), .ongoal("stay"), .width(19)) counter_1 (
    .clr(reset), .load(1'b0), .up(tl_in), .count(1'b1), .clk(clk), .D({19{1'b0}}), .Q(counter_1_q));  // open: carry
  // Probe on counter_1_q
  Comparator #(.mode("unsigned"), .width(19)) comparator_1 (
    .a(counter_1_q), .b({19{1'b1}}), .eq(comparator_1_eq));  // open: gt, lt
  Comparator #(.mode("unsigned"), .width(19)) comparator_2 (
    .a(counter_1_q), .b({19{1'b0}}), .eq(comparator_2_eq));  // open: gt, lt
  S_R_Flip_Flop s_r_ff_1 (.S(comparator_1_eq), .R(comparator_2_eq), .clk(clk), .Q(tl_out));  // open: reset, Qn, preset

  // Notes on the sheet:
  //   Internal counter value
endmodule

module debounce_sim (
  input  reset,
  input  tl_in,
  input  clk,
  output tl_out
);

  wire comparator_1_eq, comparator_2_eq;
  wire [2:0] counter_1_q;

  Counter #(.max('h7), .ongoal("stay"), .width(3)) counter_1 (
    .clr(reset), .load(1'b0), .up(tl_in), .count(1'b1), .clk(clk), .D(3'b000), .Q(counter_1_q));  // open: carry
  // Probe on counter_1_q
  Comparator #(.mode("unsigned"), .width(3)) comparator_1 (
    .a(counter_1_q), .b(3'b111), .eq(comparator_1_eq));  // open: gt, lt
  Comparator #(.mode("unsigned"), .width(3)) comparator_2 (
    .a(counter_1_q), .b(3'b000), .eq(comparator_2_eq));  // open: gt, lt
  S_R_Flip_Flop s_r_ff_1 (.S(comparator_1_eq), .R(comparator_2_eq), .clk(clk), .Q(tl_out));  // open: reset, Qn, preset

  // Notes on the sheet:
  //   Internal counter value
endmodule

module top (
  input  sw,
  input  clk_button,
  input  reset,
  output led
);

  wire clk_out, debounce_board_1_tl_out;

  Clock clk (.out(clk_out));
  debounce_board debounce_board_1 (.reset(reset), .tl_in(clk_button), .clk(clk_out), .tl_out(debounce_board_1_tl_out));
  main main_1 (.sw(sw), .clk(debounce_board_1_tl_out), .reset(reset), .led(led));
endmodule
